# Fritzing sketch wiring (saved by Fritzing 0.9.10b)

parts:
  MCU1 = Wemos Lolin32lite
  S1 = Pushbutton [package="[SMD]"]
  R1 = Resistor [tolerance=±5% power=0.25 resistance=220 package=THT]
  S2 = 0.91 inch OLED I2C Display 128 x 32 Pixels
  U1 = LIPO-110mAh [package=lipo-110]
  LED1 = smd LED [color="Red (633nm)" package="0805 [SMD]"]
  LED2 = smd LED [color="Red (633nm)" package="0805 [SMD]"]

nets:
  N1: MCU1.pin_14, U1.+
  N2: MCU1.pin_15, U1.-
  N3: MCU1.pin_23, LED1.anode
  N4: MCU1.pin_24, S1.Pin_3, S1.Pin_4, R1.Pin_1
  N5: MCU1.pin_25, S2.SCL
  N6: MCU1.pin_26, S2.SDA
  N7: MCU1.pin_28, S1.Pin_1, S1.Pin_2, S2.VCC
  N8: R1.Pin_0, LED2.cathode

notes:
  Pogo pins
  Copper rivets

custom parts:
  Wemos Lolin32lite: Wemos Lolinlite32 wifi and blue tooth board based on the ESP-32 cpu, digital I/Os 19, analog inputs 6, clock 240mhz, Flash 4Mbytes, lipo battery charger (500ma connection broken out on breadboard but not pcb), usb.
